# Fritzing sketch microbit-lm35 (saved by Fritzing 0.9.3b)
breadboards: 1

parts:
  Mod1 = Microbit
  T1 = LM35 Temperature Sensor [package="TO92 [THT]"]

nets:
  N1: Mod1.P0, T1.Vout
  N2: Mod1.3V3, T1.+Vs
  GND: Mod1.GND, T1.GND

custom parts:
  Microbit: BBC Microbit Fritzing part. May 2019 expanded to include schematic and pcb views as well as breadboard. PCB view assumes an Adafruit PRODUCT ID: 3342 2x40 Right Angle through hole edge connector (although others will probably work as well). The pcb svg is custom (see forum article http://forum.fritzing.org/t/making-edge-connectors-and-both-side-smd-parts/7287 for an explaination if you need to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
